# Fritzing sketch SchemaFritzing (saved by Fritzing 0.9.3b)
breadboards: 2

parts:
  Componente1 = Arduino Uno (Rev3)
  LED1 = smd LED [color="Green (555nm)" package="1206 [SMD]"]
  LED2 = smd LED [color="Blue (430nm)" package="1206 [SMD]"]
  LED3 = smd LED [color="Yellow (592nm)" package="1206 [SMD]"]
  LED4 = smd LED [color="Red (633nm)" package="1206 [SMD]"]
  LED5 = smd LED [color="Green (555nm)" package="1206 [SMD]"]
  J1 = Basic Servo
  R1 = Rotary Potentiometer (Small) [maximum_resistance=100kΩ package=THT]
  R2 = Resistor [tolerance=±5% resistance=220 package="2512 [SMD]"]
  R3 = Resistor [tolerance=±5% resistance=220 package="2512 [SMD]"]
  R4 = Resistor [tolerance=±5% resistance=220 package="2512 [SMD]"]
  R5 = Resistor [tolerance=±5% resistance=220 package="2512 [SMD]"]
  R6 = Resistor [tolerance=±5% resistance=220 package="2512 [SMD]"]
  Componente2 = Bluetooth HC-05 Macho
  U1 = NodeMCU V3.0

nets:
  N1: Componente1.D11_PWM/MOSI, R6.Pin_0
  N2: Componente1.D12/MISO, R5.Pin_0
  N3: Componente1.D13/SCK, R4.Pin_0
  GND: Componente1.GND, LED1.cathode, LED2.cathode, LED3.cathode, J1.gnd, Componente2.GND
  N4: Componente1.D2, Componente2.TXD
  N5: Componente1.D3_PWM, Componente2.RXD
  N6: Componente1.D7, J1.pulse
  VCC: Componente1.5V, J1.vcc, Componente2.VCC
  N7: LED1.anode, R4.Pin_1
  N8: LED2.anode, R5.Pin_1
  N9: LED3.anode, R6.Pin_1
  N10: LED4.cathode, LED5.cathode, R1.leg1, U1.GND#41
  N11: LED4.anode, R3.Pin_0
  N12: LED5.anode, R2.Pin_0
  N13: R1.wiper, U1.A0
  N14: R1.leg2, U1.VU
  N15: R2.Pin_1, U1.D0
  N16: R3.Pin_1, U1.D1
  N17: U1.GND#6, U1.GND#13, U1.GND#16, U1.GND#33

custom parts:
  NodeMCU V3.0: ESP8266 based NodeMCU
